# Fritzing sketch magloop-remote-control (saved by Fritzing 0.9.2b)

parts:
  M1 = Stepper Motor - Bipolar
  PART1 = Big Easy Driver ROB-11876 [part_number=ROB-11876]
  Power_plug1 = Power plug
  Part1 = Adafruit Bluefruit LE Shield [part_number="Adafruit #2746"]
  Parts1 = SparkFun RedBoard [part_number=DEV-12757]  # not connected

nets:
  N1: M1.A, PART1.A#0
  N2: M1.C, PART1.A#1
  N3: M1.B, PART1.B#2
  N4: M1.D, PART1.B#3
  GND: PART1.GND, Power_plug1.GND, Part1.GND
  VCC: PART1.M+, Power_plug1.VCC, Part1.VIN
  N5: PART1.SLEEP, Part1.D3
  N6: PART1.STEP, Part1.D5
  N7: PART1.DIR, Part1.D6

notes:
  Arduino to BlueFruit Shield
  Header Pins Used
  ISP BLUEFRUIT_SPI_MOSI
  ISP BLUEFRUIT_SPI_MISO
  ISP BLUEFRUIT_SPI_SCK
  D4 BLUEFRUIT_SPI_RST
  D7 BLUEFRUIT_SPI_IRQ
  D8 BLUEFRUIT_SPI_CS

custom parts:
  Big Easy Driver ROB-11876: The Big Easy Driver, designed by Brian Schmalz, is a stepper motor driver board for bi-polar stepper motors up to 1.4A/phase. It is based on the Allegro A4988 stepper driver chip. It’s the next version of the popular Easy Driver board. Each Big Easy Driver can drive up to about 1.4A per phase of a bi-polar stepper motor. It is a chopper microstepping driver which defaults to 16 step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
  Adafruit Bluefruit LE Shield: Would you like to add powerful and easy-to-use Bluetooth Low Energy to your robot, art or other electronics project? Heck yeah! With BLE now included in modern smart phones and tablets, its fun to add wireless connectivity. So what you really need is the new Adafruit Bluefruit LE Shield for Arduino! The Bluefruit LE Shield makes it easy to add Bluetooth Low Energy connectivity to your Arduino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
  SparkFun RedBoard: At SparkFun we use many Arduinos and we’re always looking for the simplest, most stable one. Each board is a bit different and no one board has everything we want, so we decided to make our own version that combines all our favorite features. The RedBoard combines the simplicity of the UNO’s Optiboot bootloader (which is used in the Pro series), the stability of the FTDI (which we all missed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
